// Logisim project s-mips.circ as structural Verilog
module S_MIPS_Board (
  input  DESHABILITAR_DISPATCHER,
  output halt
);

  wire button_1_out, CLK, CS, d_ff_1_q, LCLR, LoadRAM, LoadRAMOn, LW, R_R_W, R_W, ram_dispatcher_1_finished,
       RCS, Reset_out, RST, TTY_EN;
  wire [2:0] KDB;
  wire [3:0] LMask, Mask, ram_1_read_time, ram_1_write_time, RMask;
  wire [6:0] KDB_DATA, TTY_DATA;
  wire [15:0] Addr, LAddr, RAddr;
  wire [31:0] I0, I1, I2, I3, LData, ram_1_data_out_0, ram_1_data_out_1, ram_1_data_out_2, ram_1_data_out_3,
       RI0, RI1, RI2, RI3;

  TTY #(.rows(25), .cols(80)) tty_1 (.data(TTY_DATA), .clk(CLK), .we(TTY_EN), .clr(RST));
  not not_1 (LoadRAMOn, ram_dispatcher_1_finished);
  RAM_Dispatcher ram_dispatcher_1 (
    .WriteTime(ram_1_write_time), .Clock(CLK), .Data(LData), .Address(LAddr), .Mask(LMask),
    .Finished(ram_dispatcher_1_finished), .Write(LW), .CLR(LCLR));
  Keyboard #(.buflen(64)) keyboard_1 (.clk(CLK), .re(KDB[0]), .avail(KDB[2]), .data(KDB_DATA));  // open: clr
  RAM ram_1 (
    .Address(RAddr), .Data_Out_0(ram_1_data_out_0), .Data_Out_1(ram_1_data_out_1),
    .Data_Out_2(ram_1_data_out_2), .Data_Out_3(ram_1_data_out_3), .Data_In_0(RI0), .Data_In_1(RI1),
    .Data_In_2(RI2), .Data_In_3(RI3), .Mask(RMask), .nRead_Write(R_R_W), .Chip_Select(RCS),
    .Read_Time(ram_1_read_time), .Reset(button_1_out), .Write_Time(ram_1_write_time));
  Button button_1 (.out(button_1_out));
  D_Flip_Flop d_ff_1 (.clk(CLK), .D(1'b1), .Q(d_ff_1_q), .reset(Reset_out));  // open: Qn, preset, en
  Button Reset (.out(Reset_out));
  S_MIPS s_mips_1 (
    .Kbd_Enable(KDB[0]), .Address(Addr), .Kbd_Clear(KDB[1]), .Kbd_Available(KDB[2]), .RAM_In_0(I0),
    .Kbd_ASCII_Data(KDB_DATA), .RAM_In_1(I1), .TTY_Enable(TTY_EN), .RAM_In_2(I2), .RAM_In_3(I3),
    .TTY_ASCII_Data(TTY_DATA), .Reset(RST), .RAM_Out_0(ram_1_data_out_0), .Clock(CLK),
    .RAM_Out_1(ram_1_data_out_1), .Stop(halt), .RAM_Out_2(ram_1_data_out_2), .RAM_Out_3(ram_1_data_out_3),
    .Mask(Mask), .Read_Time(ram_1_read_time), .Write_Time(ram_1_write_time), .nRead_Write(R_W),
    .Chip_Select(CS));
  D_Flip_Flop d_ff_2 (.clk(CLK), .D(d_ff_1_q), .Qn(LCLR), .reset(Reset_out));  // open: Q, preset, en
  or or_1 (RST, LCLR, LoadRAM);
  Clock clock_1 (.out(CLK));
  Multiplexer #(.width(32), .enable("false")) multiplexer_1 (.in0(I0), .in1(LData), .out(RI0), .sel(LoadRAM));
  Multiplexer #(.width(32), .enable("false")) multiplexer_2 (.in0(I1), .in1(LData), .out(RI1), .sel(LoadRAM));
  Multiplexer #(.width(32), .enable("false")) multiplexer_3 (.in0(I2), .in1(LData), .out(RI2), .sel(LoadRAM));
  Multiplexer #(.width(32), .enable("false")) multiplexer_4 (.in0(I3), .in1(LData), .out(RI3), .sel(LoadRAM));
  and and_1 (LoadRAM, ~DESHABILITAR_DISPATCHER, LoadRAMOn);  // AND_Gate
  Multiplexer #(.width(16), .enable("false")) multiplexer_5 (.in0(Addr), .in1(LAddr), .out(RAddr), .sel(LoadRAM));
  Multiplexer #(.width(4), .enable("false")) multiplexer_6 (.in0(Mask), .in1(LMask), .out(RMask), .sel(LoadRAM));
  Multiplexer #(.enable("false")) multiplexer_7 (.in0(CS), .in1(LW), .out(RCS), .sel(LoadRAM));
  Multiplexer #(.enable("false")) multiplexer_8 (.in0(R_W), .in1(LW), .out(R_R_W), .sel(LoadRAM));

  // Notes on the sheet:
  //   NO MODIFICAR
  //   Keyboard
endmodule

module RAM (
  input  [15:0] Address,
  input  [31:0] Data_In_0,
  input  [31:0] Data_In_1,
  input  [31:0] Data_In_2,
  input  [31:0] Data_In_3,
  input  [3:0] Mask,
  input  nRead_Write,
  input  Chip_Select,
  input  Reset,
  output [31:0] Data_Out_0,
  output [31:0] Data_Out_1,
  output [31:0] Data_Out_2,
  output [31:0] Data_Out_3,
  output [3:0] Read_Time,
  output [3:0] Write_Time
);

  wire and_2_out, and_3_out, and_4_out, and_5_out, and_6_out, and_7_out, and_8_out, and_9_out, Changed, CLK,
       comparator_2_eq, comparator_3_eq, comparator_4_eq, comparator_5_eq, comparator_6_eq, Count,
       demultiplexer_3_out0, Idle, Idle_q, Load, Load0, Load1, nand_1_out, or_1_out, or_2_out, or_3_out,
       or_4_out, or_5_out, or_6_out, or_7_out, or_8_out, or_9_out, or_10_out, Proc_q, Update_Mem, Zero_Time;
  wire [3:0] counter_1_q, multiplexer_1_out, subtractor_1_out;
  wire [31:0] register_1_q, register_2_q, register_3_q, register_4_q, register_5_q;

  // Probe on 4'b0011
  // Probe on 4'b0010
  Multiplexer #(.width(4), .enable("false")) multiplexer_1 (
    .in0(4'b0011), .in1(4'b0010), .out(multiplexer_1_out), .sel(nRead_Write));
  or or_1 (or_1_out, Idle, Update_Mem);
  or or_2 (or_2_out, ~Chip_Select, Reset);  // OR_Gate
  Subtractor #(.width(4)) subtractor_1 (.a(multiplexer_1_out), .b(4'b0010), .out(subtractor_1_out));  // open: bin, bout
  Demultiplexer #(.enable("false")) demultiplexer_1 (.out0(Idle), .out1(Load0), .in(Idle_q), .sel(Changed));
  D_Flip_Flop u_Idle (.clk(CLK), .D(or_1_out), .Q(Idle_q), .preset(or_2_out));  // open: Qn, en, reset
  // Probe on counter_1_q
  Counter #(.width(4), .max('hf)) counter_1 (
    .load(Load), .D(subtractor_1_out), .count(Count), .Q(counter_1_q), .clk(CLK), .clr(or_3_out));  // open: carry
  or or_3 (or_3_out, ~Chip_Select, Reset);  // OR_Gate
  Comparator #(.width(4), .mode("unsigned")) comparator_1 (
    .a(4'b0000), .b(counter_1_q), .eq(Zero_Time));  // open: gt, lt
  or or_4 (or_4_out, Count, Load0, Load1);
  Register #(.width(32)) register_1 (.D(Data_In_0), .en(Chip_Select), .Q(register_1_q), .clk(CLK), .clr(or_5_out));
  or or_5 (or_5_out, ~Chip_Select, Reset);  // OR_Gate
  Register #(.width(32)) register_2 (.D(Data_In_1), .en(Chip_Select), .Q(register_2_q), .clk(CLK), .clr(or_6_out));
  or or_6 (or_6_out, ~Chip_Select, Reset);  // OR_Gate
  Register #(.width(32)) register_3 (.D(Data_In_2), .en(Chip_Select), .Q(register_3_q), .clk(CLK), .clr(or_7_out));
  or or_7 (or_7_out, ~Chip_Select, Reset);  // OR_Gate
  Register #(.width(32)) register_4 (.D(Data_In_3), .en(Chip_Select), .Q(register_4_q), .clk(CLK), .clr(or_8_out));
  or or_8 (or_8_out, ~Chip_Select, Reset);  // OR_Gate
  Register #(.width(32)) register_5 (
    .D({{11{1'b1}}, nRead_Write, Mask, Address}), .en(Chip_Select), .Q(register_5_q), .clk(CLK),
    .clr(or_9_out));
  or or_9 (or_9_out, ~Chip_Select, Reset);  // OR_Gate
  D_Flip_Flop Proc (.clk(CLK), .D(or_4_out), .Q(Proc_q), .reset(or_10_out));  // open: Qn, preset, en
  or or_10 (or_10_out, ~Chip_Select, Reset);  // OR_Gate
  Demultiplexer #(.enable("false")) demultiplexer_2 (
    .out0(Count), .out1(Update_Mem), .in(demultiplexer_3_out0), .sel(Zero_Time));
  Demultiplexer #(.enable("false")) demultiplexer_3 (
    .out0(demultiplexer_3_out0), .out1(Load1), .in(Proc_q), .sel(Changed));
  Clock clock_1 (.out(CLK));
  Comparator #(.width(32)) comparator_2 (.a(register_1_q), .b(Data_In_0), .eq(comparator_2_eq));  // open: gt, lt
  Comparator #(.width(32)) comparator_3 (.a(register_2_q), .b(Data_In_1), .eq(comparator_3_eq));  // open: gt, lt
  Comparator #(.width(32)) comparator_4 (.a(register_3_q), .b(Data_In_2), .eq(comparator_4_eq));  // open: gt, lt
  Comparator #(.width(32)) comparator_5 (.a(register_4_q), .b(Data_In_3), .eq(comparator_5_eq));  // open: gt, lt
  Comparator #(.width(32)) comparator_6 (
    .a(register_5_q), .b({{11{1'b1}}, nRead_Write, Mask, Address}), .eq(comparator_6_eq));  // open: gt, lt
  nand nand_1 (nand_1_out, comparator_6_eq, comparator_2_eq, comparator_3_eq, comparator_4_eq, comparator_5_eq);
  and and_1 (Changed, nand_1_out, Chip_Select);
  or or_11 (Load, Count, Load1, Load0);
  and and_2 (and_2_out, Mask[0], Update_Mem, nRead_Write);
  and and_3 (and_3_out, Mask[1], Update_Mem, nRead_Write);
  and and_4 (and_4_out, Mask[2], Update_Mem, nRead_Write);
  and and_5 (and_5_out, Mask[3], Update_Mem, nRead_Write);
  RAM_part #(.addrWidth(16), .dataWidth(32), .bus("separate")) ram_1 (
    .addr(Address), .din(Data_In_0), .data(Data_Out_0), .str(and_2_out), .sel(Chip_Select), .clk(CLK),
    .ld(and_6_out), .clr(Reset));
  and and_6 (and_6_out, ~nRead_Write, Idle);  // AND_Gate
  RAM_part #(.addrWidth(16), .dataWidth(32), .bus("separate")) ram_2 (
    .addr(Address), .din(Data_In_1), .data(Data_Out_1), .str(and_3_out), .sel(Chip_Select), .clk(CLK),
    .ld(and_7_out), .clr(Reset));
  and and_7 (and_7_out, ~nRead_Write, Idle);  // AND_Gate
  RAM_part #(.addrWidth(16), .dataWidth(32), .bus("separate")) ram_3 (
    .addr(Address), .din(Data_In_2), .data(Data_Out_2), .str(and_4_out), .sel(Chip_Select), .clk(CLK),
    .ld(and_8_out), .clr(Reset));
  and and_8 (and_8_out, ~nRead_Write, Idle);  // AND_Gate
  RAM_part #(.addrWidth(16), .dataWidth(32), .bus("separate")) ram_4 (
    .addr(Address), .din(Data_In_3), .data(Data_Out_3), .str(and_5_out), .sel(Chip_Select), .clk(CLK),
    .ld(and_9_out), .clr(Reset));
  and and_9 (and_9_out, ~nRead_Write, Idle);  // AND_Gate

  assign Read_Time = 4'b0011;
  assign Write_Time = 4'b0010;

  // Other names for the same wires on the sheet: M0 = Mask[0]; M1 = Mask[1]; M2 = Mask[2]; M3 = Mask[3];
  //   RW = nRead_Write; CLR = Reset; CS = Chip_Select; Load2 = Count

  // Notes on the sheet:
  //   NO MODIFICAR
  //   excepto quizás los valores RT y WT
  //   BANK0
  //   BANK1
  //   BANK2
  //   BANK3
endmodule

module S_MIPS (
  input  Reset,
  input  Clock,
  input  [31:0] RAM_Out_0,
  input  Kbd_Available,
  input  [6:0] Kbd_ASCII_Data,
  input  [31:0] RAM_Out_1,
  input  [31:0] RAM_Out_2,
  input  [31:0] RAM_Out_3,
  input  [3:0] Read_Time,
  input  [3:0] Write_Time,
  output Kbd_Enable,
  output Kbd_Clear,
  output [15:0] Address,
  output Stop,
  output [31:0] RAM_In_0,
  output [3:0] Mask,
  output TTY_Enable,
  output [31:0] RAM_In_1,
  output [6:0] TTY_ASCII_Data,
  output nRead_Write,
  output Chip_Select,
  output [31:0] RAM_In_2,
  output [31:0] RAM_In_3
);


  // Other names for the same wires on the sheet: CLK = Clock; CLR = Reset; CS = Chip_Select;
  //   KBD_AVAIL = Kbd_Available; KBD_CLR = Kbd_Clear; KBD_DATA[6:0] = Kbd_ASCII_Data; RAM_A[15:0] = Address;
  //   RAM_INPUT_0[31:0] = RAM_In_0; RAM_INPUT_1[31:0] = RAM_In_1; RAM_INPUT_2[31:0] = RAM_In_2;
  //   RAM_INPUT_3[31:0] = RAM_In_3; RAM_MASK[3:0] = Mask; RAM_OUTPUT_0[31:0] = RAM_Out_0;
  //   RAM_OUTPUT_1[31:0] = RAM_Out_1; RAM_OUTPUT_2[31:0] = RAM_Out_2; RAM_OUTPUT_3[31:0] = RAM_Out_3;
  //   RW = nRead_Write; TTY_DATA[6:0] = TTY_ASCII_Data

  // Notes on the sheet:
  //   Inputs RAM
  //   DATA FROM RAM
  //   RAM TIMING
  //   RAM ADDRESS
  //   DATA WRITE MASK
  //   RAM CONTROL
  //   Outputs RAM
  //   DATA TO RAM
  //   KEYBOARD
  //   SEQUENCING
  //   TTY
endmodule

module RAM_Dispatcher (
  input  [3:0] WriteTime,
  input  Clock,
  input  CLR,
  output [31:0] Data,
  output [15:0] Address,
  output [3:0] Mask,
  output Finished,
  output Write
);

  wire demultiplexer_2_out1, demultiplexer_3_out1, End, IDLE_q, IncAddr, Load, or_1_out, or_2_out, While_q,
       WriteEnd;
  wire [3:0] counter_1_q;
  wire [31:0] CurrentAddress_q;

  Counter #(.width(32), .max('hffffffff)) CurrentAddress (
    .count(IncAddr), .Q({CurrentAddress_q[31:18], Address, CurrentAddress_q[1:0]}), .clk(Clock), .clr(CLR));  // open: load, D, carry
  or or_1 (or_1_out, IncAddr, demultiplexer_3_out1, Finished);
  D_Flip_Flop IDLE (.clk(Clock), .D(or_1_out), .Q(IDLE_q), .preset(CLR));  // open: Qn, en, reset
  Demultiplexer #(.enable("false")) demultiplexer_1 (.out0(Load), .out1(Finished), .in(IDLE_q), .sel(End));
  D_Flip_Flop While (.clk(Clock), .D(or_2_out), .Q(While_q), .reset(CLR));  // open: Qn, preset, en
  or or_2 (or_2_out, Write, Load);
  RAM_part #(.addrWidth(18), .dataWidth(32)) ram_1 (
    .addr({Address, CurrentAddress_q[1:0]}), .data(Data), .clk(Clock));  // open: sel, ld, clr
  Demultiplexer #(.enable("false")) demultiplexer_2 (
    .out0(Write), .out1(demultiplexer_2_out1), .in(While_q), .sel(WriteEnd));
  Decoder #(.select(2)) decoder_1 (
    .out0(Mask[0]), .out1(Mask[1]), .out2(Mask[2]), .out3(Mask[3]), .sel(CurrentAddress_q[1:0]));  // open: en
  Demultiplexer #(.enable("false")) demultiplexer_3 (
    .out0(IncAddr), .out1(demultiplexer_3_out1), .in(demultiplexer_2_out1), .sel(End));
  Counter #(.width(4), .max('hf)) counter_1 (
    .load(Load), .D(WriteTime), .count(Write), .Q(counter_1_q), .clk(Clock));  // open: carry, clr
  Comparator #(.width(32)) comparator_1 (.a(Data), .b({32{1'b1}}), .eq(End));  // open: gt, lt
  Comparator #(.width(4)) comparator_2 (.a(4'b0000), .b(counter_1_q), .eq(WriteEnd));  // open: gt, lt

  // Other names for the same wires on the sheet: CLK = Clock; Count = Write; WT[3:0] = WriteTime
endmodule

module Datapath_Prototype (
  input  [31:0] Data_In,
  input  clk,
  input  reset,
  input  Write_Inst,
  input  Write_PC,
  input  PC_or_Address,
  input  ALUsrcA,
  input  [1:0] ALUsrcB,
  input  PCsrc,
  input  [1:0] DI_Selector,
  output [15:0] RAM_Address,
  output [31:0] Data_Out,
  output MemWrite,
  output MemToReg,
  output MemRead,
  output inm,
  output mfhi,
  output mflo
);

  wire alu_1_p4, branch_control_prototype_1_p4, instruction_decoder_1_r_w, instruction_decoder_1_rt_rd, JI,
       jmp, n, undriven, undriven_2, z;
  wire [2:0] j_type;
  wire [4:0] instruction_decoder_1_da, instruction_decoder_1_sa, instruction_decoder_1_sb, multiplexer_3_out;
  wire [5:0] op;
  wire [15:0] instruction_decoder_1_k;
  wire [25:0] address;
  wire [31:0] A_q, alu_1_p7, alu_1_p8, alu_1_p9, ALUout, branch_control_prototype_1_p3, Hi, Lo,
       multiplexer_1_out, multiplexer_2_out, multiplexer_5_out, multiplexer_6_out,
       program_counter_1_pc_output, register_file_1_a, register_file_1_b, shifter_1_out, sign_extend_1_output;
  wire [31:16] multiplexer_4_out;

  Instruction_Decoder_2 instruction_decoder_1 (
    .Instruction(Data_In), .W_ID(Write_Inst), .clk(clk), .DA(instruction_decoder_1_da), .Address(address),
    .SA(instruction_decoder_1_sa), .k(instruction_decoder_1_k), .SB(instruction_decoder_1_sb),
    .MemWrite(MemWrite), .Inmediate(inm), .MemRead(MemRead), .Op(op), .MemToReg(MemToReg), .jmp_inc(JI),
    .rt_rd(instruction_decoder_1_rt_rd), .R_W(instruction_decoder_1_r_w), .jmp(jmp), .mfhi(mfhi),
    .mflo(mflo), .rst(reset));
  // Branch_Control_Prototype branch_control_prototype_1: pin names not known; wires that end beside it: jmp, j_type, branch_control_prototype_1_p3, branch_control_prototype_1_p4
  Multiplexer #(.width(32), .enable("false")) multiplexer_1 (
    .in0(ALUout), .in1(branch_control_prototype_1_p3), .out(multiplexer_1_out), .sel(JI));
  Multiplexer #(.select(2), .width(32), .enable("false")) multiplexer_2 (
    .in0(Data_In), .in1(ALUout), .in2(Hi), .in3(Lo), .out(multiplexer_2_out), .sel(DI_Selector));
  Multiplexer #(.width(5), .enable("false")) multiplexer_3 (
    .in0(instruction_decoder_1_sb), .in1(instruction_decoder_1_da), .out(multiplexer_3_out),
    .sel(instruction_decoder_1_rt_rd));
  Program_Counter_2 program_counter_1 (
    .Jump_Branch_Direction(multiplexer_1_out), .jmp(branch_control_prototype_1_p4), .PC_Write(Write_PC),
    .PC_Output(program_counter_1_pc_output), .clk(clk), .rst(reset));
  Register_File_2 register_file_1 (
    .Data_Address(multiplexer_3_out), .DI(multiplexer_2_out), .R_W(instruction_decoder_1_r_w),
    .SA(instruction_decoder_1_sa), .SB(instruction_decoder_1_sb), .Clk(clk), .Reset(reset),
    .A(register_file_1_a), .B(register_file_1_b));
  Sign_Extend sign_extend_1 (.in_1(instruction_decoder_1_k), .Output(sign_extend_1_output));  // open: Logical
  Multiplexer #(.width(32), .enable("false")) multiplexer_4 (
    .in0(program_counter_1_pc_output), .in1(ALUout), .out({multiplexer_4_out, RAM_Address}),
    .sel(PC_or_Address));
  Register #(.width(32)) A (.D(register_file_1_a), .en(1'b1), .Q(A_q), .clk(clk), .clr(reset));
  Register #(.width(32)) B (.D(register_file_1_b), .en(1'b1), .Q(Data_Out), .clk(clk), .clr(reset));
  Shifter #(.width(32)) shifter_1 (.in(sign_extend_1_output), .\dist (5'b00010), .out(shifter_1_out));
  Multiplexer #(.width(32), .enable("false")) multiplexer_5 (
    .in0(program_counter_1_pc_output), .in1(A_q), .out(multiplexer_5_out), .sel(ALUsrcA));
  Multiplexer #(.select(2), .width(32), .enable("false")) multiplexer_6 (
    .in0(Data_Out), .in1({32{1'b0}}), .in2(sign_extend_1_output), .in3(shifter_1_out),
    .out(multiplexer_6_out), .sel(ALUsrcB));
  // ALU_2 alu_1: pin names not known; wires that end beside it: multiplexer_5_out, multiplexer_6_out, z, alu_1_p4, op, n, alu_1_p7, alu_1_p8, alu_1_p9
  Register #(.width(32)) u_ALUout (.D(alu_1_p9), .en(1'b1), .Q(ALUout), .clk(clk), .clr(reset));
  Hi_Lo hi_lo_1 (
    .Hi_In(alu_1_p8), .Lo_In(alu_1_p7), .Hi_Out(Hi), .Lo_Out(Lo), .WriteHi(undriven), .WriteLo(undriven_2),
    .clk(clk), .rst(reset));

  // Other names for the same wires on the sheet: DIsrc[1:0] = DI_Selector; MR = MemRead; MW = MemWrite;
  //   PC_ADD = PC_or_Address; rst = reset; sw[31:0] = Data_Out; W_inst = Write_Inst

  // Notes on the sheet:
  //   Inputs
  //   Data From RAM
  //   Señales del CU
  //   falta el branch
  //   decoder
  //   falta el bc completo
  //   Outputs
  //   Señales hacia el CU
  //   falta aqui el ALU decoder 
  //   los load del Hi/Lo se activarán
  //   cuando el ALU decoder marque
  //   una multiplicación o una división
endmodule

module Nuevo_Datapath (
  input  [31:0] Data_In,
  input  clk,
  input  reset,
  input  Write_Inst,
  input  Write_PC,
  input  PC_or_Address,
  input  ALUsrcA,
  input  [1:0] ALUsrcB,
  input  [3:0] ALU_Op,
  input  [2:0] Branch_Op,
  input  Logical_Inmed_Op,
  input  PCsrc,
  input  [1:0] DI_Selector,
  output [15:0] RAM_Address,
  output [31:0] Data_Out
);

  wire Hi_Lo, Inmed, JI, n, R_W, RAM_Op, rt_rd, undriven_2, undriven_3, z;
  wire [4:0] multiplexer_3_out, nuevo_instruction_decoder_1_da, nuevo_instruction_decoder_1_sa,
       nuevo_instruction_decoder_1_sb;
  wire [5:0] func, op;
  wire [15:0] Const;
  wire [25:0] address;
  wire [31:0] A_q, alu_1_hi, alu_1_lo, alu_1_out, ALUout, branch_control_prototype_1_pc_out, Hi, Lo,
       multiplexer_1_out, multiplexer_2_out, multiplexer_5_out, multiplexer_6_out,
       program_counter_1_pc_output, register_file_1_b, RS, shifter_1_out, sign_extend_1_output, undriven;
  wire [31:16] multiplexer_4_out;

  Nuevo_Instruction_Decoder nuevo_instruction_decoder_1 (
    .W_ID(Write_Inst), .Clock(clk), .Reset(reset), .DA(nuevo_instruction_decoder_1_da), .Address(address),
    .SA(nuevo_instruction_decoder_1_sa), .Constant(Const), .SB(nuevo_instruction_decoder_1_sb),
    .Instruction(Data_In), .Op_code(op), .Func_code(func));
  or or_1 (rt_rd, Inmed, RAM_Op);
  Multiplexer #(.width(32), .enable("false")) multiplexer_1 (
    .in0(ALUout), .in1(branch_control_prototype_1_pc_out), .out(multiplexer_1_out), .sel(JI));
  Branch_Control_Prototype branch_control_prototype_1 (
    .Rs(RS), .PC_in(undriven), .\const (Const), .Jump(address), .Branch_Op(Branch_Op),
    .Rs_____Rt(undriven_2), .PC_Out(branch_control_prototype_1_pc_out));
  Multiplexer #(.select(2), .width(32), .enable("false")) multiplexer_2 (
    .in0(Data_In), .in1(ALUout), .in2(Hi), .in3(Lo), .out(multiplexer_2_out), .sel(DI_Selector));
  Multiplexer #(.width(5), .enable("false")) multiplexer_3 (
    .in0(nuevo_instruction_decoder_1_sb), .in1(nuevo_instruction_decoder_1_da), .out(multiplexer_3_out),
    .sel(rt_rd));
  Program_Counter_2 program_counter_1 (
    .Jump_Branch_Direction(multiplexer_1_out), .jmp(undriven_3), .PC_Write(Write_PC),
    .PC_Output(program_counter_1_pc_output), .clk(clk), .rst(reset));
  Register_File_2 register_file_1 (
    .Data_Address(multiplexer_3_out), .DI(multiplexer_2_out), .R_W(R_W), .SA(nuevo_instruction_decoder_1_sa),
    .SB(nuevo_instruction_decoder_1_sb), .Clk(clk), .Reset(reset), .A(RS), .B(register_file_1_b));
  Sign_Extend sign_extend_1 (.in_1(Const), .Output(sign_extend_1_output), .Logical(Logical_Inmed_Op));
  Multiplexer #(.width(32), .enable("false")) multiplexer_4 (
    .in0(program_counter_1_pc_output), .in1(ALUout), .out({multiplexer_4_out, RAM_Address}),
    .sel(PC_or_Address));
  Register #(.width(32)) A (.D(RS), .en(1'b1), .Q(A_q), .clk(clk), .clr(reset));
  Register #(.width(32)) B (.D(register_file_1_b), .en(1'b1), .Q(Data_Out), .clk(clk), .clr(reset));
  Shifter #(.width(32)) shifter_1 (.in(sign_extend_1_output), .\dist (5'b00010), .out(shifter_1_out));
  Multiplexer #(.width(32), .enable("false")) multiplexer_5 (
    .in0(program_counter_1_pc_output), .in1(A_q), .out(multiplexer_5_out), .sel(ALUsrcA));
  Multiplexer #(.select(2), .width(32), .enable("false")) multiplexer_6 (
    .in0(Data_Out), .in1({32{1'b0}}), .in2(sign_extend_1_output), .in3(shifter_1_out),
    .out(multiplexer_6_out), .sel(ALUsrcB));
  ALU_2 alu_1 (
    .A(multiplexer_5_out), .B(multiplexer_6_out), .Out(alu_1_out), .Zero(z), .Neg(n), .Hi(alu_1_hi),
    .Lo(alu_1_lo), .ALU_Op(ALU_Op), .Hi_Lo_Enable(Hi_Lo));
  Register #(.width(32)) u_ALUout (.D(alu_1_out), .en(1'b1), .Q(ALUout), .clk(clk), .clr(reset));
  Hi_Lo hi_lo_1 (
    .Hi_In(alu_1_hi), .Lo_In(alu_1_lo), .Hi_Out(Hi), .Lo_Out(Lo), .WriteHi(Hi_Lo), .WriteLo(Hi_Lo),
    .clk(clk), .rst(reset));

  // Other names for the same wires on the sheet: DIsrc[1:0] = DI_Selector; Logical = Logical_Inmed_Op;
  //   PC_ADD = PC_or_Address; rst = reset; sw[31:0] = Data_Out; W_inst = Write_Inst

  // Notes on the sheet:
  //   del pdf
  //   Input
  //   Data From RAM
  //   Señales del CU
  //   Ajustar las señales del CU con
  //   las que  verdaderamente salen del circuito
  //   Las instrucciones MemToReg y similares
  //   no están concebidas en la orientación,
  //   tienen señales equivalentes en las instrucciones
  //   Output
  //   ver el enable de hi/lo que sale del CU
endmodule

module Register_File_2 (
  input  [4:0] Data_Address,
  input  [31:0] DI,
  input  R_W,
  input  [4:0] SA,
  input  [4:0] SB,
  input  Clk,
  input  Reset,
  output [31:0] A,
  output [31:0] B
);

  wire _0, _4, _8, _12, _16, _20, _24, _28, not_1_out, not_2_out;
  wire [3:1] _0___3, _4___7, _8___11, _12___15, _16___19, _20___23, _24___27, _28___31;
  wire [4:0] multiplexer_1_out;
  wire [31:0] Q0, Q1, Q2, Q3, Q4, Q5, Q6, Q7, Q8, Q9, Q10, Q11, Q12, Q13, Q14, Q15, Q16, Q17, Q18, Q19, Q20,
       Q21, Q22, Q23, Q24, Q25, Q26, Q27, Q28, Q29, Q30, Q31;

  Decoder #(.select(5)) decoder_1 (
    .out0(_0), .out1(_0___3[1]), .out2(_0___3[2]), .out3(_0___3[3]), .out4(_4), .out5(_4___7[1]),
    .out6(_4___7[2]), .out7(_4___7[3]), .out8(_8), .out9(_8___11[1]), .out10(_8___11[2]), .out11(_8___11[3]),
    .out12(_12), .out13(_12___15[1]), .out14(_12___15[2]), .out15(_12___15[3]), .out16(_16),
    .out17(_16___19[1]), .out18(_16___19[2]), .out19(_16___19[3]), .out20(_20), .out21(_20___23[1]),
    .out22(_20___23[2]), .out23(_20___23[3]), .out24(_24), .out25(_24___27[1]), .out26(_24___27[2]),
    .out27(_24___27[3]), .out28(_28), .out29(_28___31[1]), .out30(_28___31[2]), .out31(_28___31[3]),
    .sel(multiplexer_1_out), .en(1'b1));
  Multiplexer #(.width(5), .enable("false")) multiplexer_1 (
    .in0({5{1'b0}}), .in1(Data_Address), .out(multiplexer_1_out), .sel(R_W));
  Register #(.width(32)) R0 (.D({32{1'b0}}), .Q(Q0), .clk(Clk), .clr(Reset));  // open: en
  Register #(.width(32)) R31__Stack_Pointer (.D(DI), .en(_28___31[3]), .Q(Q31), .clk(Clk), .clr(Reset));
  Register #(.width(32)) register_1 (.D(DI), .en(_0___3[1]), .Q(Q1), .clk(Clk), .clr(Reset));
  Register #(.width(32)) register_2 (.D(DI), .en(_4___7[3]), .Q(Q7), .clk(Clk), .clr(Reset));
  Register #(.width(32)) register_3 (.D(DI), .en(_12___15[1]), .Q(Q13), .clk(Clk), .clr(Reset));
  Register #(.width(32)) register_4 (.D(DI), .en(_16___19[3]), .Q(Q19), .clk(Clk), .clr(Reset));
  Register #(.width(32)) register_5 (.D(DI), .en(_24___27[1]), .Q(Q25), .clk(Clk), .clr(Reset));
  Multiplexer #(.select(5), .width(32)) multiplexer_2 (
    .in0(Q0), .in1(Q1), .in2(Q2), .in3(Q3), .in4(Q4), .in5(Q5), .in6(Q6), .in7(Q7), .in8(Q8), .in9(Q9),
    .in10(Q10), .in11(Q11), .in12(Q12), .in13(Q13), .in14(Q14), .in15(Q15), .in16(Q16), .in17(Q17),
    .in18(Q18), .in19(Q19), .in20(Q20), .in21(Q21), .in22(Q22), .in23(Q23), .in24(Q24), .in25(Q25),
    .in26(Q26), .in27(Q27), .in28(Q28), .in29(Q29), .in30(Q30), .in31(Q31), .out(A), .sel(SA), .en(not_1_out));
  not not_1 (not_1_out, R_W);
  Multiplexer #(.select(5), .width(32)) multiplexer_3 (
    .in0(Q0), .in1(Q1), .in2(Q2), .in3(Q3), .in4(Q4), .in5(Q5), .in6(Q6), .in7(Q7), .in8(Q8), .in9(Q9),
    .in10(Q10), .in11(Q11), .in12(Q12), .in13(Q13), .in14(Q14), .in15(Q15), .in16(Q16), .in17(Q17),
    .in18(Q18), .in19(Q19), .in20(Q20), .in21(Q21), .in22(Q22), .in23(Q23), .in24(Q24), .in25(Q25),
    .in26(Q26), .in27(Q27), .in28(Q28), .in29(Q29), .in30(Q30), .in31(Q31), .out(B), .sel(SB), .en(not_2_out));
  not not_2 (not_2_out, R_W);
  Register #(.width(32)) register_6 (.D(DI), .en(_0___3[2]), .Q(Q2), .clk(Clk), .clr(Reset));
  Register #(.width(32)) register_7 (.D(DI), .en(_8), .Q(Q8), .clk(Clk), .clr(Reset));
  Register #(.width(32)) register_8 (.D(DI), .en(_12___15[2]), .Q(Q14), .clk(Clk), .clr(Reset));
  Register #(.width(32)) register_9 (.D(DI), .en(_20), .Q(Q20), .clk(Clk), .clr(Reset));
  Register #(.width(32)) register_10 (.D(DI), .en(_24___27[2]), .Q(Q26), .clk(Clk), .clr(Reset));
  Register #(.width(32)) register_11 (.D(DI), .en(_0___3[3]), .Q(Q3), .clk(Clk), .clr(Reset));
  Register #(.width(32)) register_12 (.D(DI), .en(_8___11[1]), .Q(Q9), .clk(Clk), .clr(Reset));
  Register #(.width(32)) register_13 (.D(DI), .en(_12___15[3]), .Q(Q15), .clk(Clk), .clr(Reset));
  Register #(.width(32)) register_14 (.D(DI), .en(_20___23[1]), .Q(Q21), .clk(Clk), .clr(Reset));
  Register #(.width(32)) register_15 (.D(DI), .en(_24___27[3]), .Q(Q27), .clk(Clk), .clr(Reset));
  Register #(.width(32)) register_16 (.D(DI), .en(_4), .Q(Q4), .clk(Clk), .clr(Reset));
  Register #(.width(32)) register_17 (.D(DI), .en(_8___11[2]), .Q(Q10), .clk(Clk), .clr(Reset));
  Register #(.width(32)) register_18 (.D(DI), .en(_16), .Q(Q16), .clk(Clk), .clr(Reset));
  Register #(.width(32)) register_19 (.D(DI), .en(_20___23[2]), .Q(Q22), .clk(Clk), .clr(Reset));
  Register #(.width(32)) register_20 (.D(DI), .en(_28), .Q(Q28), .clk(Clk), .clr(Reset));
  Register #(.width(32)) register_21 (.D(DI), .en(_4___7[1]), .Q(Q5), .clk(Clk), .clr(Reset));
  Register #(.width(32)) register_22 (.D(DI), .en(_8___11[3]), .Q(Q11), .clk(Clk), .clr(Reset));
  Register #(.width(32)) register_23 (.D(DI), .en(_16___19[1]), .Q(Q17), .clk(Clk), .clr(Reset));
  Register #(.width(32)) register_24 (.D(DI), .en(_20___23[3]), .Q(Q23), .clk(Clk), .clr(Reset));
  Register #(.width(32)) register_25 (.D(DI), .en(_28___31[1]), .Q(Q29), .clk(Clk), .clr(Reset));
  Register #(.width(32)) register_26 (.D(DI), .en(_4___7[2]), .Q(Q6), .clk(Clk), .clr(Reset));
  Register #(.width(32)) register_27 (.D(DI), .en(_12), .Q(Q12), .clk(Clk), .clr(Reset));
  Register #(.width(32)) register_28 (.D(DI), .en(_16___19[2]), .Q(Q18), .clk(Clk), .clr(Reset));
  Register #(.width(32)) register_29 (.D(DI), .en(_24), .Q(Q24), .clk(Clk), .clr(Reset));
  Register #(.width(32)) register_30 (.D(DI), .en(_28___31[2]), .Q(Q30), .clk(Clk), .clr(Reset));

  // Other names for the same wires on the sheet: _0___3[0] = _0; _1 = _0___3[1]; _2 = _0___3[2]; _3 = _0___3[3];
  //   _4___7[0] = _4; _5 = _4___7[1]; _6 = _4___7[2]; _7 = _4___7[3]; _8___11[0] = _8; _9 = _8___11[1];
  //   _10 = _8___11[2]; _11 = _8___11[3]; _12___15[0] = _12; _13 = _12___15[1]; _14 = _12___15[2]; _15 = _12___15[3];
  //   _16___19[0] = _16; _17 = _16___19[1]; _18 = _16___19[2]; _19 = _16___19[3]; _20___23[0] = _20;
  //   _21 = _20___23[1]; _22 = _20___23[2]; _23 = _20___23[3]; _24___27[0] = _24; _25 = _24___27[1];
  //   _26 = _24___27[2]; _27 = _24___27[3]; _28___31[0] = _28; _29 = _28___31[1]; _30 = _28___31[2];
  //   _31 = _28___31[3]; A_t[4:0] = SA; Address[4:0] = Data_Address; B_t[4:0] = SB; Data_A[31:0] = A;
  //   Data_B[31:0] = B; Data_In[31:0] = DI; rst = Reset

  // Notes on the sheet:
  //   Data In
  //   Read/Write
  //   Selector A
  //   Selector B
  //   Inputs
  //   Fix
  //   Controlador de Lectura
  //   Controlador de Escritura
  //   Registros 1 - 30
  //   Túneles de los loads
  //   Outputs
  //   Data A
  //   Data B
endmodule

module Register_32_bits (
  input  [31:0] Data_In,
  input  Load,
  input  Clk,
  input  Reset,
  output [31:0] Data_Out
);

  D_Flip_Flop #(.trigger("falling")) d_ff_1 (
    .clk(Clk), .D(Data_In[0]), .Q(Data_Out[0]), .en(Load), .reset(Reset));  // open: Qn, preset
  D_Flip_Flop #(.trigger("falling")) d_ff_2 (
    .clk(Clk), .D(Data_In[6]), .Q(Data_Out[6]), .en(Load), .reset(Reset));  // open: Qn, preset
  D_Flip_Flop #(.trigger("falling")) d_ff_3 (
    .clk(Clk), .D(Data_In[12]), .Q(Data_Out[12]), .en(Load), .reset(Reset));  // open: Qn, preset
  D_Flip_Flop #(.trigger("falling")) d_ff_4 (
    .clk(Clk), .D(Data_In[18]), .Q(Data_Out[18]), .en(Load), .reset(Reset));  // open: Qn, preset
  D_Flip_Flop #(.trigger("falling")) d_ff_5 (
    .clk(Clk), .D(Data_In[24]), .Q(Data_Out[24]), .en(Load), .reset(Reset));  // open: Qn, preset
  D_Flip_Flop #(.trigger("falling")) d_ff_6 (
    .clk(Clk), .D(Data_In[30]), .Q(Data_Out[30]), .en(Load), .reset(Reset));  // open: Qn, preset
  D_Flip_Flop #(.trigger("falling")) d_ff_7 (
    .clk(Clk), .D(Data_In[1]), .Q(Data_Out[1]), .en(Load), .reset(Reset));  // open: Qn, preset
  D_Flip_Flop #(.trigger("falling")) d_ff_8 (
    .clk(Clk), .D(Data_In[7]), .Q(Data_Out[7]), .en(Load), .reset(Reset));  // open: Qn, preset
  D_Flip_Flop #(.trigger("falling")) d_ff_9 (
    .clk(Clk), .D(Data_In[13]), .Q(Data_Out[13]), .en(Load), .reset(Reset));  // open: Qn, preset
  D_Flip_Flop #(.trigger("falling")) d_ff_10 (
    .clk(Clk), .D(Data_In[19]), .Q(Data_Out[19]), .en(Load), .reset(Reset));  // open: Qn, preset
  D_Flip_Flop #(.trigger("falling")) d_ff_11 (
    .clk(Clk), .D(Data_In[25]), .Q(Data_Out[25]), .en(Load), .reset(Reset));  // open: Qn, preset
  D_Flip_Flop #(.trigger("falling")) d_ff_12 (
    .clk(Clk), .D(Data_In[31]), .Q(Data_Out[31]), .en(Load), .reset(Reset));  // open: Qn, preset
  D_Flip_Flop #(.trigger("falling")) d_ff_13 (
    .clk(Clk), .D(Data_In[2]), .Q(Data_Out[2]), .en(Load), .reset(Reset));  // open: Qn, preset
  D_Flip_Flop #(.trigger("falling")) d_ff_14 (
    .clk(Clk), .D(Data_In[8]), .Q(Data_Out[8]), .en(Load), .reset(Reset));  // open: Qn, preset
  D_Flip_Flop #(.trigger("falling")) d_ff_15 (
    .clk(Clk), .D(Data_In[14]), .Q(Data_Out[14]), .en(Load), .reset(Reset));  // open: Qn, preset
  D_Flip_Flop #(.trigger("falling")) d_ff_16 (
    .clk(Clk), .D(Data_In[20]), .Q(Data_Out[20]), .en(Load), .reset(Reset));  // open: Qn, preset
  D_Flip_Flop #(.trigger("falling")) d_ff_17 (
    .clk(Clk), .D(Data_In[26]), .Q(Data_Out[26]), .en(Load), .reset(Reset));  // open: Qn, preset
  D_Flip_Flop #(.trigger("falling")) d_ff_18 (
    .clk(Clk), .D(Data_In[3]), .Q(Data_Out[3]), .en(Load), .reset(Reset));  // open: Qn, preset
  D_Flip_Flop #(.trigger("falling")) d_ff_19 (
    .clk(Clk), .D(Data_In[9]), .Q(Data_Out[9]), .en(Load), .reset(Reset));  // open: Qn, preset
  D_Flip_Flop #(.trigger("falling")) d_ff_20 (
    .clk(Clk), .D(Data_In[15]), .Q(Data_Out[15]), .en(Load), .reset(Reset));  // open: Qn, preset
  D_Flip_Flop #(.trigger("falling")) d_ff_21 (
    .clk(Clk), .D(Data_In[21]), .Q(Data_Out[21]), .en(Load), .reset(Reset));  // open: Qn, preset
  D_Flip_Flop #(.trigger("falling")) d_ff_22 (
    .clk(Clk), .D(Data_In[27]), .Q(Data_Out[27]), .en(Load), .reset(Reset));  // open: Qn, preset
  D_Flip_Flop #(.trigger("falling")) d_ff_23 (
    .clk(Clk), .D(Data_In[4]), .Q(Data_Out[4]), .en(Load), .reset(Reset));  // open: Qn, preset
  D_Flip_Flop #(.trigger("falling")) d_ff_24 (
    .clk(Clk), .D(Data_In[10]), .Q(Data_Out[10]), .en(Load), .reset(Reset));  // open: Qn, preset
  D_Flip_Flop #(.trigger("falling")) d_ff_25 (
    .clk(Clk), .D(Data_In[16]), .Q(Data_Out[16]), .en(Load), .reset(Reset));  // open: Qn, preset
  D_Flip_Flop #(.trigger("falling")) d_ff_26 (
    .clk(Clk), .D(Data_In[22]), .Q(Data_Out[22]), .en(Load), .reset(Reset));  // open: Qn, preset
  D_Flip_Flop #(.trigger("falling")) d_ff_27 (
    .clk(Clk), .D(Data_In[28]), .Q(Data_Out[28]), .en(Load), .reset(Reset));  // open: Qn, preset
  D_Flip_Flop #(.trigger("falling")) d_ff_28 (
    .clk(Clk), .D(Data_In[5]), .Q(Data_Out[5]), .en(Load), .reset(Reset));  // open: Qn, preset
  D_Flip_Flop #(.trigger("falling")) d_ff_29 (
    .clk(Clk), .D(Data_In[11]), .Q(Data_Out[11]), .en(Load), .reset(Reset));  // open: Qn, preset
  D_Flip_Flop #(.trigger("falling")) d_ff_30 (
    .clk(Clk), .D(Data_In[17]), .Q(Data_Out[17]), .en(Load), .reset(Reset));  // open: Qn, preset
  D_Flip_Flop #(.trigger("falling")) d_ff_31 (
    .clk(Clk), .D(Data_In[23]), .Q(Data_Out[23]), .en(Load), .reset(Reset));  // open: Qn, preset
  D_Flip_Flop #(.trigger("falling")) d_ff_32 (
    .clk(Clk), .D(Data_In[29]), .Q(Data_Out[29]), .en(Load), .reset(Reset));  // open: Qn, preset

  // Other names for the same wires on the sheet: _0_7[7:0] = Data_In[7:0]; D0 = Data_In[0]; D1 = Data_In[1];
  //   D2 = Data_In[2]; D3 = Data_In[3]; D4 = Data_In[4]; D5 = Data_In[5]; D6 = Data_In[6]; D7 = Data_In[7];
  //   _8_15[7:0] = Data_In[15:8]; D8 = Data_In[8]; D9 = Data_In[9]; D10 = Data_In[10]; D11 = Data_In[11];
  //   D12 = Data_In[12]; D13 = Data_In[13]; D14 = Data_In[14]; D15 = Data_In[15]; _16_23[7:0] = Data_In[23:16];
  //   D16 = Data_In[16]; D17 = Data_In[17]; D18 = Data_In[18]; D19 = Data_In[19]; D20 = Data_In[20];
  //   D21 = Data_In[21]; D22 = Data_In[22]; D23 = Data_In[23]; _24_31[7:0] = Data_In[31:24]; D24 = Data_In[24];
  //   D25 = Data_In[25]; D26 = Data_In[26]; D27 = Data_In[27]; D28 = Data_In[28]; D29 = Data_In[29];
  //   D30 = Data_In[30]; D31 = Data_In[31]; Q0 = Data_Out[0]; Q1 = Data_Out[1]; Q2 = Data_Out[2]; Q3 = Data_Out[3];
  //   Q4 = Data_Out[4]; Q5 = Data_Out[5]; Q6 = Data_Out[6]; Q7 = Data_Out[7]; Q8 = Data_Out[8]; Q9 = Data_Out[9];
  //   Q10 = Data_Out[10]; Q11 = Data_Out[11]; Q12 = Data_Out[12]; Q13 = Data_Out[13]; Q14 = Data_Out[14];
  //   Q15 = Data_Out[15]; Q16 = Data_Out[16]; Q17 = Data_Out[17]; Q18 = Data_Out[18]; Q19 = Data_Out[19];
  //   Q20 = Data_Out[20]; Q21 = Data_Out[21]; Q22 = Data_Out[22]; Q23 = Data_Out[23]; Q24 = Data_Out[24];
  //   Q25 = Data_Out[25]; Q26 = Data_Out[26]; Q27 = Data_Out[27]; Q28 = Data_Out[28]; Q29 = Data_Out[29];
  //   Q30 = Data_Out[30]; Q31 = Data_Out[31]; RST = Reset

  // Notes on the sheet:
  //   Inputs
  //   Output
endmodule

module Test_RF (
  input  [4:0] in_1,
  input  [4:0] in_2,
  input  [31:0] in_3,
  input  [4:0] in_4,
  input  in_5,
  input  in_6,
  output [31:0] out_7,
  output [31:0] out_8
);

  wire clock_1_out;

  // Probe on in_3
  Register_File_2 register_file_1 (
    .Data_Address(in_4), .DI(in_3), .R_W(in_5), .SA(in_1), .SB(in_2), .Clk(clock_1_out), .Reset(in_6),
    .A(out_7), .B(out_8));
  Clock clock_1 (.out(clock_1_out));
  // Probe on out_7
  // Probe on out_8
endmodule

module ALU_2 (
  input  [31:0] A,
  input  [31:0] B,
  input  [3:0] ALU_Op,
  output [31:0] Out,
  output Zero,
  output Neg,
  output [31:0] Hi,
  output [31:0] Lo,
  output Hi_Lo_Enable
);

  wire comparator_1_lt, comparator_2_lt;
  wire [31:0] AND, div_hi, div_lo, divu_hi, divu_lo, mul_hi, mul_lo, mulu_hi, mulu_lo, NOR, OR, tunnel,
       tunnel_t, tunnel_t_t, u, XOR;

  // Probe on A
  // Probe on B
  Adder #(.width(32)) adder_1 (.a(A), .b(B), .out(tunnel));  // open: cin, cout
  Subtractor #(.width(32)) subtractor_1 (.a(A), .b(B), .out(tunnel_t));  // open: bin, bout
  assign AND = A & B;  // AND_Gate and_1, 32 bits wide
  assign OR = A | B;  // OR_Gate or_1, 32 bits wide
  Multiplier #(.width(32)) multiplier_1 (.a(A), .b(B), .out(mulu_lo), .cout(mulu_hi));  // open: cin
  Divider #(.width(32)) divider_1 (.a(A), .b(B), .out(divu_lo), .rem(divu_hi));  // open: upper
  Comparator #(.width(32)) comparator_1 (.a(A), .b(B), .lt(comparator_1_lt));  // open: gt, eq
  Comparator #(.width(32), .mode("unsigned")) comparator_2 (.a(A), .b(B), .lt(comparator_2_lt));  // open: gt, eq
  \Multiplicación_con_Signo  \multiplicación_con_signo_1  (.A(A), .B(B), .Hi(mul_hi), .Lo(mul_lo));
  Divisor_Con_Signo divisor_con_signo_1 (.in_1(A), .in_2(B), .Lo(div_lo), .Hi(div_hi));
  assign NOR = ~(A | B);  // NOR_Gate nor_1, 32 bits wide
  assign XOR = A ^ B;  // XOR_Gate xor_1, 32 bits wide
  Multiplexer #(.width(32), .enable("false")) multiplexer_1 (
    .in0({32{1'b0}}), .in1(32'h1), .out(tunnel_t_t), .sel(comparator_1_lt));
  Multiplexer #(.width(32), .enable("false")) multiplexer_2 (
    .in0({32{1'b0}}), .in1(32'h1), .out(u), .sel(comparator_2_lt));
  Multiplexer #(.select(3), .width(32), .enable("false")) multiplexer_3 (
    .in0(tunnel), .in1(tunnel_t), .in2(AND), .in3(OR), .in4(NOR), .in5(XOR), .in6(tunnel_t_t), .in7(u),
    .out({Neg, Out[30:0]}), .sel(ALU_Op[2:0]));
  // Probe on Hi
  Multiplexer #(.select(2), .width(32), .enable("false")) multiplexer_4 (
    .in0(mul_hi), .in1(mulu_hi), .in2(div_hi), .in3(divu_hi), .out(Hi), .sel(ALU_Op[1:0]));
  Multiplexer #(.select(2), .width(32), .enable("false")) multiplexer_5 (
    .in0(mul_lo), .in1(mulu_lo), .in2(div_lo), .in3(divu_lo), .out(Lo), .sel(ALU_Op[1:0]));
  // Probe on Lo
  // Probe on {Neg, Out[30:0]}
  Comparator #(.width(32)) comparator_3 (.a({Neg, Out[30:0]}), .b({32{1'b0}}), .eq(Zero));  // open: gt, lt

  assign Hi_Lo_Enable = ALU_Op[3];
  assign Out[31] = Neg;

  // Other names for the same wires on the sheet: L = ALU_Op[3]; S[2:0] = ALU_Op[2:0]; S_Hi_Lo[1:0] = ALU_Op[1:0]

  // Notes on the sheet:
  //   Inputs
  //   Entrada A
  //   Entrada B
  //   ALU Control
  //   Operaciones Básicas
  //   Operaciones de Hi/Lo
  //   Outputs
  //   Salidas al Hi/Lo
endmodule

module Hi_Lo (
  input  [31:0] Hi_In,
  input  WriteHi,
  input  [31:0] Lo_In,
  input  WriteLo,
  input  clk,
  input  rst,
  output [31:0] Hi_Out,
  output [31:0] Lo_Out
);

  Register #(.width(32)) Hi (.D(Hi_In), .en(WriteHi), .Q(Hi_Out), .clk(clk), .clr(rst));
  Register #(.width(32)) Lo (.D(Lo_In), .en(WriteLo), .Q(Lo_Out), .clk(clk), .clr(rst));

  // Notes on the sheet:
  //   Inputs
  //   Outputs
endmodule

module \Multiplicación_con_Signo  (
  input  [31:0] A,
  input  [31:0] B,
  output [31:0] Hi,
  output [31:0] Lo
);

  wire adder_1_cout, adder_3_cout;
  wire [31:0] _00_hi, _00_lo, _01_hi, _01_lo, _10_hi, _10_lo, _11_hi, _11_lo, bit_extender_1_out,
       bit_extender_2_out, multiplier_2_cout, multiplier_2_out, multiplier_3_cout, multiplier_3_out,
       nand_1_out, nand_2_out, nand_3_out, nand_4_out, negator_1_out, negator_2_out, negator_3_out,
       negator_4_out;

  // Probe on A
  // Probe on B
  Multiplier #(.width(32)) multiplier_1 (.a(A), .b(B), .out(_00_lo), .cout(_00_hi));  // open: cin
  Negator #(.width(32)) negator_1 (.in(A), .out(negator_1_out));
  Multiplier #(.width(32)) multiplier_2 (
    .a(negator_1_out), .b(B), .out(multiplier_2_out), .cout(multiplier_2_cout));  // open: cin
  Negator #(.width(32)) negator_2 (.in(B), .out(negator_2_out));
  assign nand_1_out = ~(multiplier_2_out & {32{1'b1}});  // NAND_Gate nand_1, 32 bits wide
  assign nand_2_out = ~(multiplier_2_cout & {32{1'b1}});  // NAND_Gate nand_2, 32 bits wide
  assign bit_extender_1_out = {{31{1'b0}}, adder_1_cout};  // Bit_Extender bit_extender_1
  Multiplier #(.width(32)) multiplier_3 (
    .a(A), .b(negator_2_out), .out(multiplier_3_out), .cout(multiplier_3_cout));  // open: cin
  Adder #(.width(32)) adder_1 (.a(nand_1_out), .b(32'h1), .out(_10_lo), .cout(adder_1_cout));  // open: cin
  Adder #(.width(32)) adder_2 (.a(nand_2_out), .b(bit_extender_1_out), .out(_10_hi));  // open: cin, cout
  assign nand_3_out = ~(multiplier_3_out & {32{1'b1}});  // NAND_Gate nand_3, 32 bits wide
  assign nand_4_out = ~(multiplier_3_cout & {32{1'b1}});  // NAND_Gate nand_4, 32 bits wide
  assign bit_extender_2_out = {{31{1'b0}}, adder_3_cout};  // Bit_Extender bit_extender_2
  Negator #(.width(32)) negator_3 (.in(A), .out(negator_3_out));
  Negator #(.width(32)) negator_4 (.in(B), .out(negator_4_out));
  Adder #(.width(32)) adder_3 (.a(nand_3_out), .b(32'h1), .out(_01_lo), .cout(adder_3_cout));  // open: cin
  Adder #(.width(32)) adder_4 (.a(nand_4_out), .b(bit_extender_2_out), .out(_01_hi));  // open: cin, cout
  Multiplier #(.width(32)) multiplier_4 (
    .a(negator_3_out), .b(negator_4_out), .out(_11_lo), .cout(_11_hi));  // open: cin
  Multiplexer #(.select(2), .width(32), .enable("false")) multiplexer_1 (
    .in0(_00_hi), .in1(_01_hi), .in2(_10_hi), .in3(_11_hi), .out(Hi), .sel({A[31], B[31]}));
  Multiplexer #(.select(2), .width(32), .enable("false")) multiplexer_2 (
    .in0(_00_lo), .in1(_01_lo), .in2(_10_lo), .in3(_11_lo), .out(Lo), .sel({A[31], B[31]}));

  // Other names for the same wires on the sheet: B_Sign = B[31]; A_Sign = A[31]

  // Notes on the sheet:
  //   Inputs
  //   Ambos positivos
  //   A negativo y B positivo
  //   A positivo y B negativo
  //   Ambos negativos
  //   Outputs
endmodule

module Divisor_Con_Signo (
  input  [31:0] in_1,
  input  [31:0] in_2,
  output [31:0] Lo,
  output [31:0] Hi
);

  wire [31:0] _00, _00_hi, _01, _01_hi, _10, _10_hi, _11, _11_hi, divider_2_out, divider_2_rem,
       divider_3_out, divider_4_rem, negator_1_out, negator_4_out, negator_5_out, negator_6_out;

  // Probe on in_1
  // Probe on in_2
  Multiplexer #(.select(2), .width(32), .enable("false")) multiplexer_1 (
    .in0(_00), .in1(_01), .in2(_10), .in3(_11), .out(Lo), .sel({in_1[31], in_2[31]}));
  // Probe on Lo
  Multiplexer #(.select(2), .width(32), .enable("false")) multiplexer_2 (
    .in0(_00_hi), .in1(_01_hi), .in2(_10_hi), .in3(_11_hi), .out(Hi), .sel({in_1[31], in_2[31]}));
  // Probe on Hi
  // Probe on in_1
  // Probe on in_2
  // Probe on in_1
  // Probe on in_2
  // Probe on in_1
  // Probe on in_2
  Divider #(.width(32)) divider_1 (.a(in_1), .b(in_2), .out(_00), .rem(_00_hi));  // open: upper
  Negator #(.width(32)) negator_1 (.in(in_1), .out(negator_1_out));
  // Probe on _10_hi
  // Probe on _00
  Divider #(.width(32)) divider_2 (
    .a(negator_1_out), .b(in_2), .out(divider_2_out), .rem(divider_2_rem));  // open: upper
  // Probe on divider_2_out
  Negator #(.width(32)) negator_2 (.in(divider_2_rem), .out(_10_hi));
  Negator #(.width(32)) negator_3 (.in(divider_2_out), .out(_10));
  // Probe on in_1
  // Probe on in_2
  // Probe on _10
  Divider #(.width(32)) divider_3 (.a(in_1), .b(negator_4_out), .out(divider_3_out), .rem(_01_hi));  // open: upper
  Negator #(.width(32)) negator_4 (.in(in_2), .out(negator_4_out));
  // Probe on in_1
  // Probe on in_2
  // Probe on divider_3_out
  Negator #(.width(32)) negator_5 (.in(in_1), .out(negator_5_out));
  Negator #(.width(32)) negator_6 (.in(in_2), .out(negator_6_out));
  // Probe on _11_hi
  Negator #(.width(32)) negator_7 (.in(divider_3_out), .out(_01));
  // Probe on _01
  Divider #(.width(32)) divider_4 (
    .a(negator_5_out), .b(negator_6_out), .out(_11), .rem(divider_4_rem));  // open: upper
  Negator #(.width(32)) negator_8 (.in(divider_4_rem), .out(_11_hi));
  // Probe on _11

  // Other names for the same wires on the sheet: A[31:0] = in_1; BMS_A = in_1[31]; B[31:0] = in_2; BMS_B = in_2[31]

  // Notes on the sheet:
  //   A
  //   B
  //   Inputs
  //   Output
  //   Ambos Positivos
  //   A negativo y B positivo
  //   A positivo y B negativo
  //   Ambos Negativos
endmodule

module Test_ALU (
  input  [31:0] in_1,
  input  [3:0] in_2,
  input  [31:0] in_3,
  output out_4,
  output out_5,
  output [31:0] out_6
);

  // Probe on in_1
  // Probe on in_3
  // Probe on out_6
  // ALU_2 alu_1: pin names not known; wires that end beside it: in_1, in_3, out_4, in_2, out_5, out_6
endmodule

module Branch_Control_Prototype (
  input  [31:0] Rs,
  input  [31:0] PC_in,
  input  [15:0] \const ,
  input  [25:0] Jump,
  input  [2:0] Branch_Op,
  input  Rs_____Rt,
  output [31:0] PC_Out
);

  wire and_1_out, and_2_out, and_3_out, and_4_out, and_5_out, b_jump, beq, bgtz, blez, bltz, bne,
       comparator_1_eq, comparator_1_lt, j, jr, nop, Rs____0, Rs_____0;
  wire [1:0] jump_t;
  wire [31:0] bit_extender_1_out, Branch, multiplier_1_out, Std;
  wire [31:28] J_PC;

  Decoder #(.select(3), .disabled(0), .enable("false")) decoder_1 (
    .out0(nop), .out1(beq), .out2(bne), .out3(blez), .out4(bgtz), .out5(bltz), .out6(j), .out7(jr),
    .sel(Branch_Op));
  Comparator #(.width(32)) comparator_1 (
    .a(Rs), .b({32{1'b0}}), .eq(comparator_1_eq), .lt(comparator_1_lt));  // open: gt
  Comparator #(.width(32)) comparator_2 (.a(Rs), .b({32{1'b0}}), .lt(Rs____0));  // open: gt, eq
  and and_1 (and_1_out, beq, Rs_____Rt);
  and and_2 (and_2_out, bne, ~Rs_____Rt);  // AND_Gate
  and and_3 (and_3_out, blez, Rs_____0);
  and and_4 (and_4_out, bgtz, ~Rs_____0);  // AND_Gate
  and and_5 (and_5_out, bltz, Rs____0);
  Adder #(.width(32)) adder_1 (.a(PC_in), .b(32'h4), .out(Std));  // open: cin, cout
  assign bit_extender_1_out = {{16{\const [15]}}, \const };  // Bit_Extender bit_extender_1
  or or_1 (Rs_____0, comparator_1_eq, comparator_1_lt);
  Multiplier #(.width(32)) multiplier_1 (.a(32'h4), .b(bit_extender_1_out), .out(multiplier_1_out));  // open: cin, cout
  or or_2 (b_jump, and_1_out, and_2_out, and_3_out, and_4_out, and_5_out);
  Adder #(.width(32)) adder_2 (.a(Std), .b(multiplier_1_out), .out(Branch));  // open: cin, cout
  Priority_Encoder #(.select(2)) priority_encoder_1 (
    .in0(1'b1), .in1(b_jump), .in2(j), .in3(jr), .out(jump_t), .en_in(1'b1));  // open: gs, en_out
  BitSelector #(.width(32), .group(4)) bitselector_1 (.in(PC_in), .out(J_PC), .sel(3'b111));
  Multiplexer #(.select(2), .width(32), .disabled(0), .enable("false")) multiplexer_1 (
    .in0(Std), .in1(Branch), .in2({J_PC, Jump, 2'b00}), .in3(Rs), .out(PC_Out), .sel(jump_t));

  // Other names for the same wires on the sheet: J_PC[27:2] = Jump

  // Notes on the sheet:
  //   Input
  //   Standard Value
  //   Branch Value
  //   Op Decode
  //   B Jump
  //   Jump Encode
  //   J Jump
  //   Output
  //   Seleccionar Salto
endmodule

module Instruction_Decoder_2 (
  input  [31:0] Instruction,
  input  rst,
  input  W_ID,
  input  clk,
  output [4:0] DA,
  output [25:0] Address,
  output [4:0] SA,
  output [15:0] k,
  output [4:0] SB,
  output MemWrite,
  output Inmediate,
  output MemRead,
  output [5:0] Op,
  output MemToReg,
  output mfhi,
  output mflo,
  output jmp_inc,
  output jmp,
  output rt_rd,
  output R_W
);

  wire and_2_out, and_3_out, and_4_out, and_5_out, and_6_out, and_7_out, and_9_out, and_10_out, nor_2_out,
       or_1_out, xnor_1_out;
  wire [5:0] Op_Code;

  Register #(.width(32)) Current_Instruction (.D(Instruction), .en(W_ID), .Q({Op_Code, Address}), .clk(clk), .clr(rst));
  nor nor_1 (jmp_inc, Op_Code[0], ~Op_Code[1], Op_Code[2], Op_Code[4], Op_Code[5], Op_Code[3]);  // NOR_Gate
  and and_1 (Inmediate, ~rt_rd, ~jmp_inc);  // AND_Gate
  and and_2 (and_2_out, Op_Code[2], ~Op_Code[3]);  // AND_Gate
  xnor xnor_1 (xnor_1_out, Op_Code[3], Op_Code[5]);
  nor nor_2 (nor_2_out, Op_Code[0], Op_Code[1], Op_Code[2], Op_Code[4], Op_Code[5], Op_Code[3]);
  and and_3 (and_3_out, Op_Code[4], Op_Code[5]);
  or or_1 (or_1_out, and_2_out, xnor_1_out);
  or or_2 (rt_rd, nor_2_out, and_3_out);
  or or_3 (R_W, rt_rd, ~or_1_out);  // OR_Gate
  and and_4 (and_4_out, Op_Code[3], Op_Code[4], Op_Code[5]);
  and and_5 (and_5_out, Inmediate, Op_Code[3], Op_Code[5]);
  and and_6 (and_6_out, Inmediate, ~Op_Code[3], Op_Code[5]);  // AND_Gate
  and and_7 (and_7_out, and_4_out, rt_rd, Address[0]);
  and and_8 (MemToReg, and_4_out, ~Address[0], rt_rd);  // AND_Gate
  or or_4 (MemWrite, and_5_out, and_7_out);
  or or_5 (MemRead, and_6_out, MemToReg);
  and and_9 (and_9_out, Inmediate, and_10_out);
  and and_10 (and_10_out, ~Op_Code[3], ~Op_Code[5]);  // AND_Gate
  or or_6 (jmp, and_9_out, jmp_inc);
  and and_11 (mfhi, rt_rd, Address[4]);
  and and_12 (mflo, rt_rd, Address[4], Address[1]);

  assign DA = Address[15:11];
  assign k = Address[15:0];
  assign Op = Address[5:0];
  assign SA = Address[25:21];
  assign SB = Address[20:16];

  // Other names for the same wires on the sheet: Func_Code[5:0] = Address[5:0]; inmediate_t[15:0] = Address[15:0];
  //   rd[4:0] = Address[15:11]; rt[4:0] = Address[20:16]; rs[4:0] = Address[25:21]; I_Type = Inmediate;
  //   J_Type = jmp_inc; R_Type = rt_rd

  // Notes on the sheet:
  //   Inputs
  //   de tipo R
  //   de tipo J
  //   de tipo I
  //   Determina el tipo de instrucción
  //   Señales de control para el Register File
  //   Read/Write
  //   Registro Destino
  //   Salto incondicional
  //   Data Address
  //   Selector A
  //   Selector B
  //   Señales de control de Memoria
  //   Señales de control para el Branch Control
  //   falta el branch decoder
  //   Outputs
  //   Salto Condicional
  //   Dirección para instrucciones de jump
  //   Constante
  //   Señales de control para el ALU
  //   Selector de operando Inmediato
  //   Operación
  //   Instrucciones de Copia de Registros
endmodule

module Nuevo_Instruction_Decoder (
  input  [31:0] Instruction,
  input  W_ID,
  input  Clock,
  input  Reset,
  output [4:0] DA,
  output [25:0] Address,
  output [4:0] SA,
  output [15:0] Constant,
  output [4:0] SB,
  output [5:0] Func_code,
  output [5:0] Op_code
);

  Register #(.width(32)) Current_Instruction (
    .D(Instruction), .en(W_ID), .Q({Op_code, Address}), .clk(Clock), .clr(Reset));

  assign Constant = Address[15:0];
  assign DA = Address[15:11];
  assign Func_code = Address[5:0];
  assign SA = Address[25:21];
  assign SB = Address[20:16];

  // Other names for the same wires on the sheet: inmediate[15:0] = Address[15:0]; rd[4:0] = Address[15:11];
  //   rt[4:0] = Address[20:16]; rs[4:0] = Address[25:21]; clk = Clock; Inst[31:0] = Instruction; rst = Reset

  // Notes on the sheet:
  //   Input
  //   Data Address
  //   Selector A
  //   Selector B
  //   Op-Code
  //   Output
  //   Dirección para instrucciones de salto
  //   Constante
  //   Func-Code
endmodule

module Program_Counter_2 (
  input  [31:0] Jump_Branch_Direction,
  input  clk,
  input  rst,
  input  jmp,
  input  PC_Write,
  output [31:0] PC_Output
);

  wire [31:0] adder_1_out, multiplexer_1_out;

  Adder #(.width(32)) adder_1 (.a(PC_Output), .b(32'h4), .out(adder_1_out));  // open: cin, cout
  Multiplexer #(.width(32), .enable("false")) multiplexer_1 (
    .in0(adder_1_out), .in1(Jump_Branch_Direction), .out(multiplexer_1_out), .sel(jmp));
  Register #(.width(32)) PC (.D(multiplexer_1_out), .en(PC_Write), .Q(PC_Output), .clk(clk), .clr(rst));

  // Notes on the sheet:
  //   Inputs
  //   Output
endmodule

module Control_Unit_Prototype (
  input  [5:0] Op_code,
  input  [5:0] Func_code,
  input  [3:0] Read_Time,
  input  [3:0] Write_Time,
  input  Clk,
  input  Reset,
  output [3:0] ALU_Op,
  output [2:0] Branch_Op,
  output Inmediate_Op,
  output Logical_Inmed_Op,
  output Hi_Lo_Op,
  output mfhi,
  output Rand,
  output KBD_DP,
  output lw,
  output Stack_Op,
  output pop,
  output SP,
  output KBD_ENABLE,
  output TTY_ENABLE,
  output Chip_Select,
  output RW_RAM,
  output Load_PC,
  output Load_Instuction,
  output Unsigned,
  output R___W,
  output RAM_Op,
  output END
);

  wire CS_0, CS_1, CS_2, CS_3, CS_4, d_ff_1_q, d_ff_3_q, d_ff_8_q, demultiplexer_1_out0,
       demultiplexer_1_out1, demultiplexer_2_out0, demultiplexer_3_out0, demultiplexer_3_out4,
       demultiplexer_3_out6, demultiplexer_4_out0, demultiplexer_4_out1, demultiplexer_5_out1,
       demultiplexer_6_out0, demultiplexer_7_out0, demultiplexer_7_out1, demultiplexer_8_out0,
       demultiplexer_9_out0, demultiplexer_9_out1, demultiplexer_10_out0, IDLE_q, lw_t, nor_1_out, not_1_out,
       or_7_out, or_8_out, or_9_out, or_10_out, or_11_out, or_12_out, pop_t, R___W_1, SP2, Stack_Op_t, Wait,
       WAIT_q;
  wire [1:0] Sp_Op;
  wire [2:0] CU_Op;
  wire [3:0] counter_1_q, RT____WT;

  Multiplexer #(.width(4), .enable("false")) multiplexer_1 (
    .in0(Read_Time), .in1(Write_Time), .out(RT____WT), .sel(RW_RAM));
  or or_1 (Chip_Select, CS_0, CS_1, CS_4, CS_2, CS_3);
  or or_2 (RW_RAM, CS_1, CS_4);
  Operation_Decoder operation_decoder_1 (
    .Op_code(Op_code), .Func_code(Func_code), .CU_Operation(CU_Op), .ALU_Operation(ALU_Op),
    .Branch_Operation(Branch_Op), .Special_Operation(Sp_Op), .pop(pop_t), .mfhi(mfhi), .lw(lw_t),
    .Logical_Inmed_Op(Logical_Inmed_Op), .Unsigned(Unsigned));
  D_Flip_Flop d_ff_1 (.clk(Clk), .D(Chip_Select), .Q(d_ff_1_q), .reset(Reset));  // open: Qn, preset, en
  or or_3 (R___W, R___W_1, Inmediate_Op, Hi_Lo_Op, lw, pop, KBD_DP, Rand);
  Counter #(.width(4), .max('hf)) counter_1 (
    .load(Chip_Select), .D(RT____WT), .count(d_ff_1_q), .Q(counter_1_q), .clk(Clk));  // open: carry, clr
  nor nor_1 (nor_1_out, counter_1_q[0], counter_1_q[1], counter_1_q[2], counter_1_q[3]);
  and and_1 (Wait, nor_1_out, d_ff_1_q);
  or or_4 (Stack_Op, CS_4, CS_3);
  or or_5 (RAM_Op, CS_1, CS_2);
  or or_6 (SP, pop, SP2);
  Demultiplexer #(.disabled(0), .enable("false")) demultiplexer_1 (
    .out0(demultiplexer_1_out0), .out1(demultiplexer_1_out1), .in(IDLE_q), .sel(not_1_out));
  D_Flip_Flop IDLE (.clk(Clk), .D(demultiplexer_1_out0), .Q(IDLE_q), .preset(Reset));  // open: Qn, en, reset
  not not_1 (not_1_out, Reset);
  or or_7 (or_7_out, demultiplexer_2_out0, d_ff_8_q, demultiplexer_1_out1);
  D_Flip_Flop d_ff_2 (.clk(Clk), .D(or_7_out), .Q(CS_0), .reset(Reset));  // open: Qn, preset, en
  Demultiplexer #(.enable("false")) demultiplexer_2 (
    .out0(demultiplexer_2_out0), .out1(Load_Instuction), .in(CS_0), .sel(Wait));
  D_Flip_Flop d_ff_3 (.clk(Clk), .D(Load_Instuction), .Q(d_ff_3_q), .reset(Reset));  // open: Qn, preset, en
  Demultiplexer #(.select(3), .disabled(0), .enable("false")) demultiplexer_3 (
    .out0(demultiplexer_3_out0), .out1(R___W_1), .out2(Inmediate_Op), .out3(Hi_Lo_Op),
    .out4(demultiplexer_3_out4), .out5(Stack_Op_t), .out6(demultiplexer_3_out6), .in(d_ff_3_q), .sel(CU_Op));  // open: out7
  Demultiplexer #(.disabled(0), .enable("false")) demultiplexer_4 (
    .out0(demultiplexer_4_out0), .out1(demultiplexer_4_out1), .in(demultiplexer_3_out4), .sel(lw_t));
  Demultiplexer #(.disabled(0), .enable("false")) demultiplexer_5 (
    .out0(SP2), .out1(demultiplexer_5_out1), .in(Stack_Op_t), .sel(pop_t));
  Demultiplexer #(.select(2), .disabled(0), .enable("false")) demultiplexer_6 (
    .out0(demultiplexer_6_out0), .out1(Rand), .out2(KBD_DP), .out3(TTY_ENABLE), .in(demultiplexer_3_out6),
    .sel(Sp_Op));
  or or_8 (or_8_out, demultiplexer_7_out0, demultiplexer_4_out0);
  or or_9 (or_9_out, demultiplexer_8_out0, demultiplexer_4_out1);
  or or_10 (or_10_out, END, demultiplexer_6_out0);
  D_Flip_Flop d_ff_4 (.clk(Clk), .D(or_8_out), .Q(CS_1), .reset(Reset));  // open: Qn, preset, en
  D_Flip_Flop d_ff_5 (.clk(Clk), .D(or_9_out), .Q(CS_2), .reset(Reset));  // open: Qn, preset, en
  or or_11 (or_11_out, demultiplexer_9_out0, SP2);
  or or_12 (or_12_out, demultiplexer_10_out0, demultiplexer_5_out1);
  D_Flip_Flop u_END (.clk(Clk), .D(or_10_out), .Q(END), .reset(Reset));  // open: Qn, preset, en
  D_Flip_Flop d_ff_6 (.clk(Clk), .D(or_11_out), .Q(CS_4), .reset(Reset));  // open: Qn, preset, en
  D_Flip_Flop d_ff_7 (.clk(Clk), .D(or_12_out), .Q(CS_3), .reset(Reset));  // open: Qn, preset, en
  Demultiplexer #(.enable("false")) demultiplexer_7 (
    .out0(demultiplexer_7_out0), .out1(demultiplexer_7_out1), .in(CS_1), .sel(Wait));
  Demultiplexer #(.enable("false")) demultiplexer_8 (.out0(demultiplexer_8_out0), .out1(lw), .in(CS_2), .sel(Wait));
  D_Flip_Flop u_WAIT (.clk(Clk), .D(TTY_ENABLE), .Q(WAIT_q), .reset(Reset));  // open: Qn, preset, en
  Demultiplexer #(.enable("false")) demultiplexer_9 (
    .out0(demultiplexer_9_out0), .out1(demultiplexer_9_out1), .in(CS_4), .sel(Wait));
  Demultiplexer #(.enable("false")) demultiplexer_10 (.out0(demultiplexer_10_out0), .out1(pop), .in(CS_3), .sel(Wait));
  D_Flip_Flop WAIT_2 (.clk(Clk), .D(KBD_DP), .Q(KBD_ENABLE), .reset(Reset));  // open: Qn, preset, en
  or or_13 (Load_PC, demultiplexer_3_out0, R___W_1, Inmediate_Op, Hi_Lo_Op, demultiplexer_7_out1, lw, demultiplexer_9_out1, pop, Rand, KBD_ENABLE, WAIT_q);
  D_Flip_Flop d_ff_8 (.clk(Clk), .D(Load_PC), .Q(d_ff_8_q), .reset(Reset));  // open: Qn, preset, en

  // Other names for the same wires on the sheet: CS = Chip_Select; Load_Inst = Load_Instuction;
  //   Inmedaite = Inmediate_Op; R___W_2 = Inmediate_Op; R___W_3 = Hi_Lo_Op; R___W_5 = KBD_DP; R___W_6 = Rand;
  //   R_W = R___W; R_W_RAM_1 = CS_1; RAM_Op_1 = CS_1; RAM_Op_2 = CS_2; RT[3:0] = Read_Time; R___W_7 = lw; S_lw = lw;
  //   R___W_4 = pop; S_pop = pop; SP1 = pop; R_W_RAM_2 = CS_4; Stack_Op_1 = CS_4; Stack_Op_2 = CS_3;
  //   WT[3:0] = Write_Time

  // Notes on the sheet:
  //   Input
  //   Op/Func Decode
  //   Wait
  //   Disjunction
  //   Inmediate Operation
  //   Register Operation
  //   RAM Operation
  //   Stack Operation
  //   Special Operation
  //   Branch Operation
  //   ALU Operation
  //   Store word
  //   Load word
  //   Push
  //   Pop
  //   Output
endmodule

module Operation_Decoder (
  input  [5:0] Op_code,
  input  [5:0] Func_code,
  output [2:0] CU_Operation,
  output [3:0] ALU_Operation,
  output [2:0] Branch_Operation,
  output [1:0] Special_Operation,
  output pop,
  output mfhi,
  output lw,
  output Logical_Inmed_Op,
  output Unsigned
);

  wire add, addi, AL_Op, \and , and_5_out, and_6_out, and_7_out, and_8_out, and_9_out, and_10_out,
       and_17_out, and_18_out, and_19_out, and_20_out, and_21_out, and_22_out, and_29_out, and_30_out,
       and_31_out, and_35_out, and_37_out, and_39_out, and_41_out, and_42_out, and_43_out, and_59_out,
       and_63_out, andi, beq, bgtz, blez, bltz, bne, Branch_Op, div, divu, F_000000, halt, Inmed_Op, j, jr,
       kbd, mflo, mult, Mult_Div_Op, mulu, nop, \nor , O_000000, O_111000, O_111111, \or , or_11_out,
       or_12_out, or_13_out, or_14_out, or_15_out, or_16_out, or_17_out, ori, push, RAM_Op, Register_Op, rnd,
       sliti, slitiu, slt, sltu, Special_Op, Stack_Op, sub, sw, tty, \xor , xori;

  and and_1 (O_000000, ~Op_code[0], ~Op_code[1], ~Op_code[2], ~Op_code[3], ~Op_code[4], ~Op_code[5]);  // AND_Gate
  and and_2 (O_111000, ~Op_code[0], ~Op_code[1], ~Op_code[2], Op_code[3], Op_code[4], Op_code[5]);  // AND_Gate
  and and_3 (O_111111, Op_code[0], Op_code[1], Op_code[2], Op_code[3], Op_code[4], Op_code[5]);
  and and_4 (F_000000, ~Func_code[0], ~Func_code[1], ~Func_code[2], ~Func_code[3], ~Func_code[4], ~Func_code[5]);  // AND_Gate
  and and_5 (and_5_out, ~Func_code[0], ~Func_code[1], ~Func_code[2], ~Func_code[3], ~Func_code[4], Func_code[5]);  // AND_Gate
  and and_6 (and_6_out, ~Func_code[0], Func_code[1], ~Func_code[2], ~Func_code[3], ~Func_code[4], Func_code[5]);  // AND_Gate
  and and_7 (and_7_out, ~Func_code[0], ~Func_code[1], ~Func_code[2], Func_code[3], Func_code[4], ~Func_code[5]);  // AND_Gate
  and and_8 (and_8_out, Func_code[0], ~Func_code[1], ~Func_code[2], Func_code[3], Func_code[4], ~Func_code[5]);  // AND_Gate
  and and_9 (and_9_out, ~Func_code[0], Func_code[1], ~Func_code[2], Func_code[3], Func_code[4], ~Func_code[5]);  // AND_Gate
  and and_10 (and_10_out, Func_code[0], Func_code[1], ~Func_code[2], Func_code[3], Func_code[4], ~Func_code[5]);  // AND_Gate
  and and_11 (add, and_5_out, O_000000);
  and and_12 (sub, and_6_out, O_000000);
  and and_13 (mult, and_7_out, O_000000);
  and and_14 (mulu, and_8_out, O_000000);
  and and_15 (div, and_9_out, O_000000);
  and and_16 (divu, and_10_out, O_000000);
  and and_17 (and_17_out, ~Func_code[0], Func_code[1], ~Func_code[2], Func_code[3], ~Func_code[4], Func_code[5]);  // AND_Gate
  and and_18 (and_18_out, Func_code[0], Func_code[1], ~Func_code[2], Func_code[3], ~Func_code[4], Func_code[5]);  // AND_Gate
  and and_19 (and_19_out, ~Func_code[0], ~Func_code[1], Func_code[2], ~Func_code[3], ~Func_code[4], Func_code[5]);  // AND_Gate
  and and_20 (and_20_out, Func_code[0], ~Func_code[1], Func_code[2], ~Func_code[3], ~Func_code[4], Func_code[5]);  // AND_Gate
  and and_21 (and_21_out, Func_code[0], Func_code[1], Func_code[2], ~Func_code[3], ~Func_code[4], Func_code[5]);  // AND_Gate
  and and_22 (and_22_out, ~Func_code[0], ~Func_code[1], ~Func_code[2], Func_code[3], ~Func_code[4], Func_code[5]);  // AND_Gate
  and and_23 (slt, and_17_out, O_000000);
  and and_24 (sltu, and_18_out, O_000000);
  and and_25 (\and , and_19_out, O_000000);
  and and_26 (\or , and_20_out, O_000000);
  and and_27 (\nor , and_21_out, O_000000);
  and and_28 (\xor , and_22_out, O_000000);
  and and_29 (and_29_out, ~Func_code[0], ~Func_code[1], ~Func_code[2], Func_code[3], ~Func_code[4], ~Func_code[5]);  // AND_Gate
  and and_30 (and_30_out, ~Func_code[0], ~Func_code[1], ~Func_code[2], ~Func_code[3], Func_code[4], ~Func_code[5]);  // AND_Gate
  and and_31 (and_31_out, ~Func_code[0], Func_code[1], ~Func_code[2], ~Func_code[3], Func_code[4], ~Func_code[5]);  // AND_Gate
  and and_32 (jr, and_29_out, O_000000);
  and and_33 (mfhi, and_30_out, O_000000);
  and and_34 (mflo, and_31_out, O_000000);
  and and_35 (and_35_out, ~Func_code[0], ~Func_code[1], ~Func_code[2], ~Func_code[3], ~Func_code[4], ~Func_code[5]);  // AND_Gate
  and and_36 (pop, and_35_out, O_111000);
  and and_37 (and_37_out, Func_code[0], ~Func_code[1], ~Func_code[2], ~Func_code[3], ~Func_code[4], ~Func_code[5]);  // AND_Gate
  and and_38 (push, and_37_out, O_111000);
  and and_39 (and_39_out, Func_code[0], Func_code[1], Func_code[2], Func_code[3], Func_code[4], Func_code[5]);
  and and_40 (halt, and_39_out, O_111111);
  and and_41 (and_41_out, ~Func_code[0], Func_code[1], ~Func_code[2], ~Func_code[3], ~Func_code[4], ~Func_code[5]);  // AND_Gate
  and and_42 (and_42_out, ~Func_code[0], ~Func_code[1], Func_code[2], ~Func_code[3], ~Func_code[4], ~Func_code[5]);  // AND_Gate
  and and_43 (and_43_out, Func_code[0], ~Func_code[1], ~Func_code[2], ~Func_code[3], ~Func_code[4], ~Func_code[5]);  // AND_Gate
  and and_44 (rnd, and_41_out, O_111111);
  and and_45 (kbd, and_42_out, O_111111);
  and and_46 (tty, and_43_out, O_111111);
  and and_47 (addi, ~Op_code[0], ~Op_code[1], ~Op_code[2], Op_code[3], ~Op_code[4], ~Op_code[5]);  // AND_Gate
  and and_48 (sliti, ~Op_code[0], Op_code[1], ~Op_code[2], Op_code[3], ~Op_code[4], ~Op_code[5]);  // AND_Gate
  and and_49 (slitiu, Op_code[0], Op_code[1], ~Op_code[2], Op_code[3], ~Op_code[4], ~Op_code[5]);  // AND_Gate
  and and_50 (andi, ~Op_code[0], ~Op_code[1], Op_code[2], Op_code[3], ~Op_code[4], ~Op_code[5]);  // AND_Gate
  and and_51 (ori, Op_code[0], ~Op_code[1], Op_code[2], Op_code[3], ~Op_code[4], ~Op_code[5]);  // AND_Gate
  and and_52 (xori, ~Op_code[0], Op_code[1], Op_code[2], Op_code[3], ~Op_code[4], ~Op_code[5]);  // AND_Gate
  and and_53 (beq, ~Op_code[0], ~Op_code[1], Op_code[2], ~Op_code[3], ~Op_code[4], ~Op_code[5]);  // AND_Gate
  and and_54 (bne, Op_code[0], ~Op_code[1], Op_code[2], ~Op_code[3], ~Op_code[4], ~Op_code[5]);  // AND_Gate
  and and_55 (blez, ~Op_code[0], Op_code[1], Op_code[2], ~Op_code[3], ~Op_code[4], ~Op_code[5]);  // AND_Gate
  and and_56 (bgtz, Op_code[0], Op_code[1], Op_code[2], ~Op_code[3], ~Op_code[4], ~Op_code[5]);  // AND_Gate
  and and_57 (bltz, Op_code[0], ~Op_code[1], ~Op_code[2], ~Op_code[3], ~Op_code[4], ~Op_code[5]);  // AND_Gate
  and and_58 (j, ~Op_code[0], Op_code[1], ~Op_code[2], ~Op_code[3], ~Op_code[4], ~Op_code[5]);  // AND_Gate
  and and_59 (and_59_out, ~Op_code[0], ~Op_code[1], ~Op_code[2], ~Op_code[3], ~Op_code[4], ~Op_code[5]);  // AND_Gate
  and and_60 (nop, and_59_out, F_000000);
  and and_61 (lw, Op_code[0], Op_code[1], ~Op_code[2], ~Op_code[3], ~Op_code[4], Op_code[5]);  // AND_Gate
  and and_62 (sw, Op_code[0], Op_code[1], ~Op_code[2], Op_code[3], ~Op_code[4], Op_code[5]);  // AND_Gate
  or or_1 (Logical_Inmed_Op, andi, ori, xori);
  or or_2 (Special_Op, halt, rnd, kbd, tty);
  or or_3 (Stack_Op, pop, push);
  or or_4 (RAM_Op, lw, sw);
  or or_5 (Register_Op, mfhi, mflo);
  or or_6 (Mult_Div_Op, mult, mulu, div, divu);
  or or_7 (Unsigned, mult, div);
  or or_8 (AL_Op, add, sub, mult, mulu, div, divu, slt, sltu, \and , \or , \nor , \xor );
  or or_9 (Branch_Op, nop, beq, bne, blez, bgtz, bltz, j, jr);
  or or_10 (Inmed_Op, addi, sliti, slitiu, andi, ori, xori);
  or or_11 (or_11_out, add, addi);
  or or_12 (or_12_out, \and , andi);
  or or_13 (or_13_out, \or , ori);
  or or_14 (or_14_out, \xor , xori);
  or or_15 (or_15_out, slt, sliti);
  or or_16 (or_16_out, sltu, slitiu);
  or or_17 (or_17_out, halt, 1'b1);
  and and_63 (and_63_out, ~AL_Op, ~Inmed_Op);  // AND_Gate
  Priority_Encoder #(.select(2), .disabled(0)) priority_encoder_1 (
    .in0(or_17_out), .in1(rnd), .in2(kbd), .in3(tty), .out(Special_Operation), .en_in(1'b1));  // open: gs, en_out
  Priority_Encoder #(.disabled(0)) priority_encoder_2 (
    .in0(Branch_Op), .in1(AL_Op), .in2(Inmed_Op), .in3(Register_Op), .in4(RAM_Op), .in5(Stack_Op),
    .in6(Special_Op), .out(CU_Operation), .en_in(1'b1));  // open: in7, gs, en_out
  Priority_Encoder #(.select(4), .disabled(0)) priority_encoder_3 (
    .in0(or_11_out), .in1(sub), .in2(or_12_out), .in3(or_13_out), .in4(\nor ), .in5(or_14_out),
    .in6(or_15_out), .in7(or_16_out), .in8(mult), .in9(mulu), .in10(div), .in11(divu), .in15(and_63_out),
    .out(ALU_Operation), .en_in(1'b1));  // open: in12, in13, in14, gs, en_out
  Priority_Encoder #(.disabled(0)) priority_encoder_4 (
    .in0(1'b1), .in1(beq), .in2(bne), .in3(blez), .in4(bgtz), .in5(bltz), .in6(j), .in7(jr),
    .out(Branch_Operation), .en_in(1'b1));  // open: gs, en_out

  // Notes on the sheet:
  //   Input
  //   Códigos
  //   para instrucciones de tipo R
  //   No Operation
  //   ALU
  //   Func-code Decode
  //   Register
  //   Stack
  //   Special
  //   ALU
  //   Op-code Decode
  //   Branch
  //   RAM
  //   Operaciones
  //   Output / Encode op
  //   Control Unit
  //   ALU
  //   Branch
  //   Special
  //   Otras
endmodule

module RAM_Manager (
  input  [31:0] in_1,
  input  [31:0] RAM_O0,
  input  [31:0] RAM_O1,
  input  [31:0] RAM_In,
  input  [31:0] RAM_O2,
  input  [31:0] RAM_O3,
  output [3:0] Mask,
  output [15:0] Address_Out,
  output [31:0] RAM_O0_2,
  output [31:0] RAM_O1_2,
  output [31:0] RAM_Out,
  output [31:0] RAM_O2_2,
  output [31:0] RAM_O3_2
);

  wire [31:16] shifter_1_out;

  // Probe on in_1
  Shifter #(.width(32), .shift("lr")) shifter_1 (.in(in_1), .\dist (5'b00010), .out({shifter_1_out, Address_Out}));
  // Probe on Address_Out
  Multiplexer #(.select(2), .width(32), .enable("false")) multiplexer_1 (
    .in0(RAM_O0), .in1(RAM_O1), .in2(RAM_O2), .in3(RAM_O3),
    .out({RAM_Out[7:0], RAM_Out[15:8], RAM_Out[23:16], RAM_Out[31:24]}), .sel(Address_Out[3:2]));
  Decoder #(.select(2), .enable("false")) decoder_1 (
    .out0(Mask[0]), .out1(Mask[1]), .out2(Mask[2]), .out3(Mask[3]), .sel(Address_Out[3:2]));

  assign RAM_O0_2 = {RAM_In[7:0], RAM_In[15:8], RAM_In[23:16], RAM_In[31:24]};
  assign RAM_O1_2 = {RAM_In[7:0], RAM_In[15:8], RAM_In[23:16], RAM_In[31:24]};
  assign RAM_O2_2 = {RAM_In[7:0], RAM_In[15:8], RAM_In[23:16], RAM_In[31:24]};
  assign RAM_O3_2 = {RAM_In[7:0], RAM_In[15:8], RAM_In[23:16], RAM_In[31:24]};

  // Other names for the same wires on the sheet: Bank[1:0] = Address_Out[3:2]

  // Notes on the sheet:
  //   Address In
  //   Solo se va a acceder a un banco a la vez
endmodule

module Sign_Extend (
  input  [15:0] in_1,
  input  Logical,
  output [31:0] Output
);

  wire [31:0] bit_extender_1_out, bit_extender_2_out;

  // Probe on in_1
  assign bit_extender_1_out = {{16{in_1[15]}}, in_1};  // Bit_Extender bit_extender_1
  Multiplexer #(.width(32), .enable("false")) multiplexer_1 (
    .in0(bit_extender_1_out), .in1(bit_extender_2_out), .out(Output), .sel(Logical));
  assign bit_extender_2_out = {{16{1'b0}}, in_1};  // Bit_Extender bit_extender_2
  // Probe on Output

  // Other names for the same wires on the sheet: Op = Logical

  // Notes on the sheet:
  //   Input
  //   Extensión con signo si es aritmética
  //   Extensión con 0 si es una operación lógica
  //   Ouput
endmodule
